# Fritzing sketch Fritizing (saved by Fritzing 0.9.4)
breadboards: 1

parts:
  Componente2 = Bluetooth HC-05 Macho  # not connected
  Componente3 = RFID USB Reader
  LED1 = smd LED [color="Red (633nm)" package="0603 [SMD]"]
  LED2 = smd LED [color="Green (555nm)" package="0603 [SMD]"]
  R2 = Resistor [tolerance=±5% resistance=220 package="0603 [SMD]"]
  R3 = Resistor [tolerance=±5% resistance=220 package="0603 [SMD]"]
  Componente1 = Arduino Uno (Rev3)
  U1 = MLX90614 [package=to-39]

nets:
  N1: Componente3.GNDT, Componente1.D10_PWM/SS
  N2: Componente3.CP, Componente1.D13/SCK
  N3: Componente3.ANT2, Componente1.D11_PWM/MOSI
  N4: Componente3.ANT1, Componente1.D12/MISO
  N5: Componente3.TX-O, Componente1.GND
  N6: Componente3.GND, Componente1.D9_PWM
  VCC: Componente3.VCC, Componente1.3V3
  N7: LED1.cathode, LED2.cathode
  N8: LED1.anode, R3.Pin_1
  N9: LED2.anode, R2.Pin_1
  N10: Componente1.D7, U1.VSS
